// Logisim project MUX.circ as structural Verilog: 3 circuits, main circuit 2-to-1 MUX
module main (
  input  in_1,
  input  in_2,
  input  in_3,
  input  in_4,
  input  in_5,
  input  in_6,
  input  in_7,
  input  in_8,
  input  in_9,
  output out_10,
  output out_11
);

  _2_to_1_MUX u_2_to_1_mux_1 (.in_1(in_1), .in_2(in_2), .in_3(in_3), .out_4(out_10));
  _4_to_1_MUX u_4_to_1_mux_1 (
    .in_1(in_4), .in_2(in_5), .in_3(in_6), .in_4(in_7), .in_5(in_8), .in_6(in_9), .out_7(out_11));
endmodule

module _2_to_1_MUX (
  input  in_1,
  input  in_2,
  input  in_3,
  output out_4
);

  wire and_1_out, and_2_out, not_1_out;

  not not_1 (not_1_out, in_3);
  and and_1 (and_1_out, in_1, not_1_out);
  and and_2 (and_2_out, in_2, in_3);
  or or_1 (out_4, and_1_out, and_2_out);
endmodule

module _4_to_1_MUX (
  input  in_1,
  input  in_2,
  input  in_3,
  input  in_4,
  input  in_5,
  input  in_6,
  output out_7
);

  wire n2_to_1_mux_1_out_4, n2_to_1_mux_2_out_4;

  _2_to_1_MUX u_2_to_1_mux_1 (.in_1(in_1), .in_2(in_2), .in_3(in_3), .out_4(n2_to_1_mux_1_out_4));
  _2_to_1_MUX u_2_to_1_mux_2 (.in_1(in_4), .in_2(in_5), .in_3(in_3), .out_4(n2_to_1_mux_2_out_4));
  _2_to_1_MUX u_2_to_1_mux_3 (.in_1(n2_to_1_mux_1_out_4), .in_2(n2_to_1_mux_2_out_4), .in_3(in_6), .out_4(out_7));
endmodule
