// Logisim project XOR_AddMachine.circ as structural Verilog: 3 circuits, main circuit main
module main (
  input  in_1,
  input  in_2,
  output out_3,
  output [7:0] out_4,
  output [7:0] out_5
);

  XOR xor_1 (.in_1(in_1), .in_2(in_2), .out_3(out_3));
  Add_Machine add_machine_1 (.out_1(out_4), .out_2(out_5));
endmodule

module XOR (
  input  in_1,
  input  in_2,
  output out_3
);

  wire and_1_out, and_2_out, not_1_out, not_2_out;

  not not_1 (not_1_out, in_2);
  not not_2 (not_2_out, in_1);
  and and_1 (and_1_out, in_1, not_1_out);
  and and_2 (and_2_out, not_2_out, not_2_out, in_2);
  or or_1 (out_3, and_1_out, and_2_out);
endmodule

module Add_Machine (
  output [7:0] out_1,
  output [7:0] out_2
);

  wire clock_1_out;

  Register register_1 (.D(out_1), .Q(out_2), .clk(clock_1_out));  // open: en, clr
  Clock clock_1 (.out(clock_1_out));
  Adder adder_1 (.a(8'h1), .b(out_2), .out(out_1));  // open: cin, cout
endmodule
