// Logisim project lab6.circ as structural Verilog
module Ex_1 (
  input  [7:0] \input ,
  output Out1,
  output [7:0] Out2
);

  not not_1 (Out2[7], \input [7]);
  and and_1 (Out1, \input [0], \input [7]);

  assign Out2[6:0] = \input [6:0];
endmodule

module rotr (
  input  [15:0] A,
  input  [3:0] B,
  output [15:0] \output 
);

  wire [3:0] not_1_out;
  wire [15:0] multiplexer_1_out, multiplexer_2_out, multiplexer_3_out, n1bit_shift_1_out_2,
       n2bit_shift_1_out_2, n4bit_shift_1_out_2, n8bit_shift_1_out_2;

  _1bit_shift u_1bit_shift_1 (.in_1(A), .out_2(n1bit_shift_1_out_2));
  assign not_1_out = ~B;  // NOT_Gate not_1, 4 bits wide
  Multiplexer #(.width(16)) multiplexer_1 (
    .in0(n1bit_shift_1_out_2), .in1(A), .out(multiplexer_1_out), .sel(not_1_out[0]));  // open: en
  _2bit_shift u_2bit_shift_1 (.in_1(multiplexer_1_out), .out_2(n2bit_shift_1_out_2));
  Multiplexer #(.width(16)) multiplexer_2 (
    .in0(n2bit_shift_1_out_2), .in1(multiplexer_1_out), .out(multiplexer_2_out), .sel(not_1_out[1]));  // open: en
  _4bit_shift u_4bit_shift_1 (.in_1(multiplexer_2_out), .out_2(n4bit_shift_1_out_2));
  Multiplexer #(.width(16)) multiplexer_3 (
    .in0(n4bit_shift_1_out_2), .in1(multiplexer_2_out), .out(multiplexer_3_out), .sel(not_1_out[2]));  // open: en
  _8bit_shift u_8bit_shift_1 (.in_1(multiplexer_3_out), .out_2(n8bit_shift_1_out_2));
  Multiplexer #(.width(16)) multiplexer_4 (
    .in0(n8bit_shift_1_out_2), .in1(multiplexer_3_out), .out(\output ), .sel(not_1_out[3]));  // open: en
endmodule

// 1bit
module _1bit_shift (
  input  [15:0] in_1,
  output [15:0] out_2
);


  assign out_2 = {in_1[0], in_1[15:1]};
endmodule

// 2bit
module _2bit_shift (
  input  [15:0] in_1,
  output [15:0] out_2
);


  assign out_2 = {in_1[1:0], in_1[15:2]};
endmodule

// 4bit
module _4bit_shift (
  input  [15:0] in_1,
  output [15:0] out_2
);


  assign out_2 = {in_1[3:0], in_1[15:4]};
endmodule

// 8bit
module _8bit_shift (
  input  [15:0] in_1,
  output [15:0] out_2
);


  assign out_2 = {in_1[7:0], in_1[15:8]};
endmodule
