// Logisim project cpu.circ as structural Verilog: 3 circuits, main circuit main
module main (
  input  [31:0] INSTRUCTION,
  input  CLOCK,
  output [31:0] FETCH_ADDRESS,
  output [31:0] s0_Value,
  output [31:0] s1_Value,
  output [31:0] s2_Value,
  output [31:0] ra_Value,
  output [31:0] sp_Value,
  output [31:0] HI_Value,
  output [31:0] LO_Value
);

  wire ALUSrc, and_1_out, and_2_out, beqinc, comparator_1_eq, comparator_2_eq, comparator_3_eq, cutoff,
       equal, ExtOp, lui, main_2_signed_overflow, MemtoReg, MemWr, mfhi, mflo, or_1_out, RegWr, shift;
  wire [1:0] nPC_sel, RegDst;
  wire [3:0] ALUctr;
  wire [4:0] multiplexer_2_out;
  wire [25:0] address;
  wire [27:0] bit_extender_2_out, PC_4;
  wire [31:0] adder_3_out, alu1, alu2, bit_extender_1_out, bit_extender_3_out, bit_extender_4_out,
       bit_extender_5_out, BranchAddr, hi_in, JumpAddr, main_2_result, multiplexer_1_out, multiplexer_3_out,
       multiplexer_4_out, multiplexer_5_out, multiplexer_6_out, multiplexer_7_out, multiplexer_8_out,
       multiplexer_9_out, multiplexer_10_out, multiplexer_11_out, RAM, shifter_1_out, write, write_data;
  wire [31:26] newInstruction;

  control control_1 (
    .opcode(newInstruction), .\function (address[5:0]), .equal(equal), .RegDst(RegDst), .RegWr(RegWr),
    .ExtOp(ExtOp), .ALUSrc(ALUSrc), .MemWr(MemWr), .MemtoReg(MemtoReg), .ALUctr(ALUctr), .nPC_sel(nPC_sel),
    .cutoff(cutoff), .shift(shift), .lui(lui), .mfhi(mfhi), .mflo(mflo), .beqinc(beqinc));
  Register #(.width(32)) register_1 (
    .D(multiplexer_1_out), .Q({newInstruction, address}), .clk(CLOCK));  // open: en, clr
  Multiplexer #(.width(32)) multiplexer_1 (
    .in0(INSTRUCTION), .in1({32{1'b0}}), .out(multiplexer_1_out), .sel(cutoff));  // open: en
  // Probe on multiplexer_1_out
  Multiplexer #(.select(2), .width(5)) multiplexer_2 (
    .in0(address[20:16]), .in1(address[15:11]), .in2({5{1'b1}}), .out(multiplexer_2_out), .sel(RegDst));  // open: in3, en
  assign bit_extender_1_out = {{16{address[15]}}, address[15:0]};  // Bit_Extender bit_extender_1
  assign bit_extender_2_out = {{2{1'b0}}, address};  // Bit_Extender bit_extender_2
  Shifter #(.width(32)) shifter_1 (.in(bit_extender_1_out), .\dist (5'b00010), .out(shifter_1_out));
  Shifter #(.width(28)) shifter_2 (.in(bit_extender_2_out), .\dist (5'b00010), .out(JumpAddr[27:0]));
  // Probe on {JumpAddr[31:28], PC_4}
  regfile_main main_1 (
    .Read_Register_1(address[25:21]), .Read_Register_2(address[20:16]), .Write_Register(multiplexer_2_out),
    .Write_Data(write), .Write_Enable(RegWr), .Clock(CLOCK), .Read_Data_1(alu1), .Read_Data_2(alu2),
    .s0_Value(s0_Value), .s1_Value(s1_Value), .s2_Value(s2_Value), .ra_Value(ra_Value), .sp_Value(sp_Value));
  Adder #(.width(32)) adder_1 (.a(FETCH_ADDRESS), .b(shifter_1_out), .out(BranchAddr));  // open: cin, cout
  // Probe on JumpAddr
  assign bit_extender_3_out = {{16{1'b0}}, address[15:0]};  // Bit_Extender bit_extender_3
  Multiplexer #(.width(32)) multiplexer_3 (
    .in0(bit_extender_3_out), .in1(bit_extender_4_out), .out(multiplexer_3_out), .sel(ExtOp));  // open: en
  assign bit_extender_4_out = {{16{address[15]}}, address[15:0]};  // Bit_Extender bit_extender_4
  assign bit_extender_5_out = {{27{1'b0}}, address[10:6]};  // Bit_Extender bit_extender_5
  Multiplexer #(.width(32)) multiplexer_4 (
    .in0(alu2), .in1(multiplexer_3_out), .out(multiplexer_4_out), .sel(ALUSrc));  // open: en
  Multiplexer #(.width(32)) multiplexer_5 (
    .in0(alu1), .in1(bit_extender_5_out), .out(multiplexer_5_out), .sel(shift));  // open: en
  Multiplexer #(.select(2), .width(32)) multiplexer_6 (
    .in0({JumpAddr[31:28], PC_4}), .in1(BranchAddr), .in2(JumpAddr), .in3(alu1), .out(multiplexer_6_out),
    .sel(nPC_sel));  // open: en
  Register #(.width(32)) PC (.D(multiplexer_6_out), .Q(FETCH_ADDRESS), .clk(CLOCK));  // open: en, clr
  // Probe on multiplexer_6_out
  Multiplexer #(.width(32)) multiplexer_7 (
    .in0(multiplexer_5_out), .in1(32'h10), .out(multiplexer_7_out), .sel(lui));  // open: en
  Adder #(.width(32)) adder_2 (.a(32'h4), .b(FETCH_ADDRESS), .out({JumpAddr[31:28], PC_4}));  // open: cin, cout
  LED led_1 (.in(main_2_signed_overflow));
  alu_main main_2 (
    .Switch(ALUctr), .X(multiplexer_7_out), .Equal(equal), .Result(main_2_result),
    .Signed_Overflow(main_2_signed_overflow), .Y(multiplexer_4_out), .Result_2(hi_in));
  // mem_main MEM: pin names not known; wires that end beside it: main_2_result, alu2, MemWr, CLOCK, RAM
  Comparator #(.width(2)) comparator_1 (.a(RegDst), .b(2'b10), .eq(comparator_1_eq));  // open: gt, lt
  Multiplexer #(.width(32)) multiplexer_8 (
    .in0(main_2_result), .in1(RAM), .out(multiplexer_8_out), .sel(MemtoReg));  // open: en
  Multiplexer #(.width(32)) multiplexer_9 (
    .in0(write_data), .in1(FETCH_ADDRESS), .out(multiplexer_9_out), .sel(comparator_1_eq));  // open: en
  Comparator #(.width(4)) comparator_2 (.a(ALUctr), .b(4'b0011), .eq(comparator_2_eq));  // open: gt, lt
  Comparator #(.width(4)) comparator_3 (.a(ALUctr), .b(4'b0100), .eq(comparator_3_eq));  // open: gt, lt
  Adder #(.width(32)) adder_3 (.a(32'h1), .b(alu2), .out(adder_3_out));  // open: cin, cout
  Register #(.width(32)) HI (.D(hi_in), .en(or_1_out), .Q(HI_Value), .clk(CLOCK));  // open: clr
  or or_1 (or_1_out, comparator_2_eq, comparator_3_eq);
  Multiplexer #(.width(32)) multiplexer_10 (
    .in0(multiplexer_8_out), .in1(adder_3_out), .out(multiplexer_10_out), .sel(and_1_out));  // open: en
  and and_1 (and_1_out, beqinc, ~equal);  // AND_Gate
  Multiplexer #(.width(32)) multiplexer_11 (
    .in0(multiplexer_9_out), .in1(HI_Value), .out(multiplexer_11_out), .sel(mfhi));  // open: en
  Multiplexer #(.width(32)) multiplexer_12 (
    .in0(multiplexer_10_out), .in1(alu2), .out(write_data), .sel(and_2_out));  // open: en
  and and_2 (and_2_out, beqinc, equal);
  Multiplexer #(.width(32)) multiplexer_13 (
    .in0(multiplexer_11_out), .in1(LO_Value), .out(write), .sel(mflo));  // open: en
  Register #(.width(32)) LO (.D(write_data), .en(or_1_out), .Q(LO_Value), .clk(CLOCK));  // open: clr

  // Other names for the same wires on the sheet: clk = CLOCK; fetch_addr[31:0] = FETCH_ADDRESS;
  //   PC[31:0] = FETCH_ADDRESS; hi[31:0] = HI_Value; PC_4[31:28] = JumpAddr[31:28]; lo[31:0] = LO_Value;
  //   funct[5:0] = address[5:0]; immediate[15:0] = address[15:0]; newInstruction[25:0] = address;
  //   shamt[4:0] = address[10:6]; rd[4:0] = address[15:11]; rt[4:0] = address[20:16]; rs[4:0] = address[25:21];
  //   opcode[5:0] = newInstruction; ra[31:0] = ra_Value; s0[31:0] = s0_Value; s1[31:0] = s1_Value;
  //   s2[31:0] = s2_Value; sp[31:0] = sp_Value

  // Notes on the sheet:
  //   Output
  //   These are outputs/inputs from run.circ
  //   Inputs
  //   These are DEBUG/TEST outputs from your circuit.
endmodule

module old_control (
  input  equal,
  input  [5:0] opcode,
  input  [5:0] funct,
  output [1:0] RegDst,
  output RegWr,
  output ExtOp,
  output ALUSrc,
  output MemWr,
  output MemtoReg,
  output [3:0] ALUctr,
  output [1:0] nPC_sel,
  output cutoff,
  output shift,
  output lui,
  output mfhi,
  output mflo,
  output beqinc
);

  wire add, addi, addiu, addu, \and , and_7_out, and_8_out, and_9_out, and_10_out, and_11_out, andi, beq,
       branch, comparator_2_eq, comparator_3_eq, comparator_4_eq, comparator_6_eq, comparator_7_eq, divu, j,
       j_type, jal, jalr, jump, jumpreg, mult, \nor , not_1_out, not_2_out, not_5_out, not_6_out, not_7_out,
       not_8_out, \or , or_2_out, or_3_out, or_4_out, or_5_out, or_6_out, or_7_out, or_8_out, or_9_out,
       or_10_out, or_11_out, or_12_out, or_13_out, ori, r_type, sll, slt, slti, sltiu, sltu, sra, srl, sub,
       subu, \xor , xori;

  Comparator #(.width(6)) comparator_1 (.a(opcode), .b({6{1'b0}}), .eq(r_type));  // open: gt, lt
  or or_1 (j_type, j, jal);
  Comparator #(.width(6)) comparator_2 (.a(funct), .b({6{1'b0}}), .eq(comparator_2_eq));  // open: gt, lt
  Comparator #(.width(6)) comparator_3 (.a(funct), .b(6'b000010), .eq(comparator_3_eq));  // open: gt, lt
  Comparator #(.width(6)) comparator_4 (.a(funct), .b(6'b000011), .eq(comparator_4_eq));  // open: gt, lt
  Comparator #(.width(6)) comparator_5 (.a(funct), .b(6'b001000), .eq(beqinc));  // open: gt, lt
  Comparator #(.width(6)) comparator_6 (.a(funct), .b(6'b001001), .eq(comparator_6_eq));  // open: gt, lt
  Comparator #(.width(6)) comparator_7 (.a(funct), .b(6'b010000), .eq(comparator_7_eq));  // open: gt, lt
  Comparator #(.width(6)) comparator_8 (.a(funct), .b(6'b010010), .eq(mflo));  // open: gt, lt
  Comparator #(.width(6)) comparator_9 (.a(funct), .b(6'b011000), .eq(mult));  // open: gt, lt
  Comparator #(.width(6)) comparator_10 (.a(funct), .b(6'b011011), .eq(divu));  // open: gt, lt
  Comparator #(.width(6)) comparator_11 (.a(funct), .b(6'b100000), .eq(add));  // open: gt, lt
  Comparator #(.width(6)) comparator_12 (.a(funct), .b(6'b100001), .eq(addu));  // open: gt, lt
  Comparator #(.width(6)) comparator_13 (.a(funct), .b(6'b100010), .eq(sub));  // open: gt, lt
  Comparator #(.width(6)) comparator_14 (.a(funct), .b(6'b100011), .eq(subu));  // open: gt, lt
  Comparator #(.width(6)) comparator_15 (.a(funct), .b(6'b100100), .eq(\and ));  // open: gt, lt
  Comparator #(.width(6)) comparator_16 (.a(funct), .b(6'b100101), .eq(\or ));  // open: gt, lt
  and and_1 (sll, r_type, comparator_2_eq);
  and and_2 (srl, r_type, comparator_3_eq);
  and and_3 (sra, r_type, comparator_4_eq);
  and and_4 (jalr, r_type, comparator_6_eq);
  and and_5 (mfhi, r_type, comparator_7_eq);
  not not_1 (not_1_out, r_type);
  not not_2 (not_2_out, j_type);
  Comparator #(.width(6)) comparator_17 (.a(funct), .b(6'b100110), .eq(\xor ));  // open: gt, lt
  Comparator #(.width(6)) comparator_18 (.a(funct), .b(6'b100111), .eq(\nor ));  // open: gt, lt
  Comparator #(.width(6)) comparator_19 (.a(funct), .b(6'b101010), .eq(slt));  // open: gt, lt
  Comparator #(.width(6)) comparator_20 (.a(funct), .b(6'b101011), .eq(sltu));  // open: gt, lt
  Comparator #(.width(6)) comparator_21 (.a(opcode), .b(6'b000010), .eq(j));  // open: gt, lt
  Comparator #(.width(6)) comparator_22 (.a(opcode), .b(6'b000011), .eq(jal));  // open: gt, lt
  Comparator #(.width(6)) comparator_23 (.a(opcode), .b(6'b000100), .eq(beq));  // open: gt, lt
  Comparator #(.width(6)) comparator_24 (.a(opcode), .b(6'b000101), .eq(beq));  // open: gt, lt
  Comparator #(.width(6)) comparator_25 (.a(opcode), .b(6'b000110), .eq(beqinc));  // open: gt, lt
  Comparator #(.width(6)) comparator_26 (.a(opcode), .b(6'b001000), .eq(addi));  // open: gt, lt
  Comparator #(.width(6)) comparator_27 (.a(opcode), .b(6'b001001), .eq(addiu));  // open: gt, lt
  Comparator #(.width(6)) comparator_28 (.a(opcode), .b(6'b001010), .eq(slti));  // open: gt, lt
  Comparator #(.width(6)) comparator_29 (.a(opcode), .b(6'b001011), .eq(sltiu));  // open: gt, lt
  Comparator #(.width(6)) comparator_30 (.a(opcode), .b(6'b001100), .eq(andi));  // open: gt, lt
  Comparator #(.width(6)) comparator_31 (.a(opcode), .b(6'b001101), .eq(ori));  // open: gt, lt
  Comparator #(.width(6)) comparator_32 (.a(opcode), .b(6'b001110), .eq(xori));  // open: gt, lt
  Comparator #(.width(6)) comparator_33 (.a(opcode), .b(6'b001111), .eq(lui));  // open: gt, lt
  Comparator #(.width(6)) comparator_34 (.a(opcode), .b(6'b100011), .eq(MemtoReg));  // open: gt, lt
  Comparator #(.width(6)) comparator_35 (.a(opcode), .b(6'b101011), .eq(MemWr));  // open: gt, lt
  and and_6 (ALUSrc, not_1_out, not_2_out);
  or or_2 (or_2_out, jal, jalr);
  Multiplexer #(.width(2)) multiplexer_1 (.in1(2'b00), .out(RegDst), .sel(and_7_out), .en(and_7_out));  // open: in0
  and and_7 (and_7_out, ~r_type, ~jalr, ~jal);  // AND_Gate
  Multiplexer #(.width(2)) multiplexer_2 (.in1(2'b01), .out(RegDst), .sel(r_type), .en(r_type));  // open: in0
  Multiplexer #(.width(2)) multiplexer_3 (.in1(2'b10), .out(RegDst), .sel(or_2_out), .en(or_2_out));  // open: in0
  or or_3 (or_3_out, beq, beq, j, beqinc, MemWr);
  not not_3 (RegWr, or_3_out);
  not not_4 (ExtOp, or_4_out);
  or or_4 (or_4_out, ori, andi);
  not not_5 (not_5_out, branch);
  or or_5 (or_5_out, lui, sll);
  or or_6 (or_6_out, MemtoReg, add, MemWr, addi);
  assign nPC_sel = and_8_out ? 2'b00 : 2'bz;  // Controlled_Buffer controlled_buffer_1
  and and_8 (and_8_out, not_5_out, not_6_out, not_7_out);
  not not_6 (not_6_out, jumpreg);
  not not_7 (not_7_out, jump);
  assign nPC_sel = branch ? 2'b01 : 2'bz;  // Controlled_Buffer controlled_buffer_2
  assign nPC_sel = jump ? 2'b10 : 2'bz;  // Controlled_Buffer controlled_buffer_3
  assign nPC_sel = jumpreg ? 2'b11 : 2'bz;  // Controlled_Buffer controlled_buffer_4
  assign ALUctr = or_5_out ? 4'b0000 : 4'bz;  // Controlled_Buffer controlled_buffer_5
  assign ALUctr = srl ? 4'b0001 : 4'bz;  // Controlled_Buffer controlled_buffer_6
  assign ALUctr = sra ? 4'b0010 : 4'bz;  // Controlled_Buffer controlled_buffer_7
  assign ALUctr = mult ? 4'b0011 : 4'bz;  // Controlled_Buffer controlled_buffer_8
  assign ALUctr = divu ? 4'b0100 : 4'bz;  // Controlled_Buffer controlled_buffer_9
  assign ALUctr = or_6_out ? 4'b0101 : 4'bz;  // Controlled_Buffer controlled_buffer_10
  or or_7 (or_7_out, addu, addiu, and_9_out);
  and and_9 (and_9_out, beqinc, ~equal);  // AND_Gate
  assign ALUctr = sub ? 4'b0111 : 4'bz;  // Controlled_Buffer controlled_buffer_11
  assign ALUctr = subu ? 4'b1000 : 4'bz;  // Controlled_Buffer controlled_buffer_12
  assign ALUctr = or_8_out ? 4'b1001 : 4'bz;  // Controlled_Buffer controlled_buffer_13
  or or_8 (or_8_out, \and , andi);
  assign ALUctr = or_9_out ? 4'b1010 : 4'bz;  // Controlled_Buffer controlled_buffer_14
  or or_9 (or_9_out, \or , ori);
  assign ALUctr = or_7_out ? 4'b0110 : 4'bz;  // Controlled_Buffer controlled_buffer_15
  or or_10 (or_10_out, beq, beqinc);
  and and_10 (and_10_out, or_10_out, equal);
  not not_8 (not_8_out, equal);
  assign ALUctr = or_11_out ? 4'b1011 : 4'bz;  // Controlled_Buffer controlled_buffer_16
  or or_11 (or_11_out, \xor , xori);
  assign ALUctr = \nor  ? 4'b1100 : 4'bz;  // Controlled_Buffer controlled_buffer_17
  assign ALUctr = or_12_out ? 4'b1101 : 4'bz;  // Controlled_Buffer controlled_buffer_18
  or or_12 (or_12_out, slt, slti);
  or or_13 (or_13_out, sltu, sltiu);
  or or_14 (branch, and_10_out, and_11_out);
  and and_11 (and_11_out, beq, not_8_out);
  assign ALUctr = or_13_out ? 4'b1110 : 4'bz;  // Controlled_Buffer controlled_buffer_19
  or or_15 (cutoff, beq, beq, j, jal, beqinc, beqinc);
  or or_16 (jump, j, jal);
  or or_17 (jumpreg, beqinc, jalr);
  or or_18 (shift, sll, sra, srl);

  // Other names for the same wires on the sheet: aluctrl[3:0] = ALUctr; bne = beq; i_type = ALUSrc; jr = beqinc;
  //   lw = MemtoReg; sw = MemWr
endmodule

module control (
  input  [5:0] opcode,
  input  [5:0] \function ,
  input  equal,
  output [1:0] RegDst,
  output RegWr,
  output ExtOp,
  output ALUSrc,
  output MemWr,
  output MemtoReg,
  output [3:0] ALUctr,
  output [1:0] nPC_sel,
  output cutoff,
  output shift,
  output lui,
  output mfhi,
  output mflo,
  output beqinc
);

  wire add, addi, addiu, addu, \and , and_7_out, and_8_out, and_9_out, and_10_out, and_11_out, andi, beq,
       bne, branch, comparator_1_eq, comparator_2_eq, comparator_3_eq, comparator_4_eq, comparator_5_eq,
       comparator_6_eq, divu, increment, j, j_type, jal, jalr, jr, jump, jumpreg, mult, \nor , not_1_out,
       not_4_out, not_5_out, \or , or_2_out, or_3_out, or_4_out, or_6_out, or_7_out, or_8_out, or_9_out,
       or_13_out, or_14_out, or_16_out, or_17_out, or_18_out, ori, r_type, sll, slt, slti, sltiu, sltu, sra,
       srl, sub, subu, \xor , xori;

  Comparator #(.width(6)) comparator_1 (.a(\function ), .b({6{1'b0}}), .eq(comparator_1_eq));  // open: gt, lt
  Comparator #(.width(6)) comparator_2 (.a(opcode), .b({6{1'b0}}), .eq(comparator_2_eq));  // open: gt, lt
  Comparator #(.width(6)) comparator_3 (.a(\function ), .b(6'b000010), .eq(comparator_3_eq));  // open: gt, lt
  Comparator #(.width(6)) comparator_4 (.a(\function ), .b(6'b000011), .eq(comparator_4_eq));  // open: gt, lt
  Comparator #(.width(6)) comparator_5 (.a(\function ), .b(6'b001000), .eq(comparator_5_eq));  // open: gt, lt
  Comparator #(.width(6)) comparator_6 (.a(\function ), .b(6'b001001), .eq(comparator_6_eq));  // open: gt, lt
  Comparator #(.width(6)) comparator_7 (.a(opcode), .b({6{1'b0}}), .eq(r_type));  // open: gt, lt
  and and_1 (sll, comparator_1_eq, comparator_2_eq);
  and and_2 (srl, r_type, comparator_3_eq);
  and and_3 (sra, r_type, comparator_4_eq);
  and and_4 (jr, r_type, comparator_5_eq);
  and and_5 (jalr, r_type, comparator_6_eq);
  Comparator #(.width(6)) comparator_8 (.a(\function ), .b(6'b010000), .eq(mfhi));  // open: gt, lt
  Comparator #(.width(6)) comparator_9 (.a(\function ), .b(6'b010010), .eq(mflo));  // open: gt, lt
  Comparator #(.width(6)) comparator_10 (.a(\function ), .b(6'b011000), .eq(mult));  // open: gt, lt
  Comparator #(.width(6)) comparator_11 (.a(\function ), .b(6'b011011), .eq(divu));  // open: gt, lt
  Comparator #(.width(6)) comparator_12 (.a(\function ), .b(6'b100000), .eq(add));  // open: gt, lt
  Comparator #(.width(6)) comparator_13 (.a(\function ), .b(6'b100001), .eq(addu));  // open: gt, lt
  Comparator #(.width(6)) comparator_14 (.a(\function ), .b(6'b100010), .eq(sub));  // open: gt, lt
  Comparator #(.width(6)) comparator_15 (.a(\function ), .b(6'b100011), .eq(subu));  // open: gt, lt
  Comparator #(.width(6)) comparator_16 (.a(\function ), .b(6'b100100), .eq(\and ));  // open: gt, lt
  Comparator #(.width(6)) comparator_17 (.a(\function ), .b(6'b100101), .eq(\or ));  // open: gt, lt
  or or_1 (j_type, j, jal);
  Comparator #(.width(6)) comparator_18 (.a(\function ), .b(6'b100110), .eq(\xor ));  // open: gt, lt
  Comparator #(.width(6)) comparator_19 (.a(\function ), .b(6'b100111), .eq(\nor ));  // open: gt, lt
  Comparator #(.width(6)) comparator_20 (.a(\function ), .b(6'b101010), .eq(slt));  // open: gt, lt
  Comparator #(.width(6)) comparator_21 (.a(\function ), .b(6'b101011), .eq(sltu));  // open: gt, lt
  Comparator #(.width(6)) comparator_22 (.a(opcode), .b(6'b000010), .eq(j));  // open: gt, lt
  Comparator #(.width(6)) comparator_23 (.a(opcode), .b(6'b000011), .eq(jal));  // open: gt, lt
  Comparator #(.width(6)) comparator_24 (.a(opcode), .b(6'b000100), .eq(beq));  // open: gt, lt
  Comparator #(.width(6)) comparator_25 (.a(opcode), .b(6'b000101), .eq(bne));  // open: gt, lt
  Comparator #(.width(6)) comparator_26 (.a(opcode), .b(6'b000110), .eq(beqinc));  // open: gt, lt
  Comparator #(.width(6)) comparator_27 (.a(opcode), .b(6'b001000), .eq(addi));  // open: gt, lt
  Comparator #(.width(6)) comparator_28 (.a(opcode), .b(6'b001001), .eq(addiu));  // open: gt, lt
  Comparator #(.width(6)) comparator_29 (.a(opcode), .b(6'b001010), .eq(slti));  // open: gt, lt
  Comparator #(.width(6)) comparator_30 (.a(opcode), .b(6'b001011), .eq(sltiu));  // open: gt, lt
  Comparator #(.width(6)) comparator_31 (.a(opcode), .b(6'b001100), .eq(andi));  // open: gt, lt
  Comparator #(.width(6)) comparator_32 (.a(opcode), .b(6'b001101), .eq(ori));  // open: gt, lt
  Comparator #(.width(6)) comparator_33 (.a(opcode), .b(6'b001110), .eq(xori));  // open: gt, lt
  Comparator #(.width(6)) comparator_34 (.a(opcode), .b(6'b001111), .eq(lui));  // open: gt, lt
  Comparator #(.width(6)) comparator_35 (.a(opcode), .b(6'b100011), .eq(MemtoReg));  // open: gt, lt
  Comparator #(.width(6)) comparator_36 (.a(opcode), .b(6'b101011), .eq(MemWr));  // open: gt, lt
  and and_6 (ALUSrc, ~r_type, ~j_type);  // AND_Gate
  assign RegDst = r_type ? 2'b01 : 2'bz;  // Controlled_Buffer controlled_buffer_1
  assign RegDst = or_2_out ? 2'b10 : 2'bz;  // Controlled_Buffer controlled_buffer_2
  or or_2 (or_2_out, jal, jalr);
  assign RegDst = and_7_out ? 2'b00 : 2'bz;  // Controlled_Buffer controlled_buffer_3
  and and_7 (and_7_out, ~jal, ~jalr, ~r_type);  // AND_Gate
  not not_1 (not_1_out, branch);
  not not_2 (RegWr, or_3_out);
  or or_3 (or_3_out, beq, bne, j, jr, MemWr, and_8_out);
  and and_8 (and_8_out, beqinc, equal);
  or or_4 (or_4_out, ori, xori, andi);
  not not_3 (ExtOp, or_4_out);
  assign nPC_sel = and_9_out ? 2'b00 : 2'bz;  // Controlled_Buffer controlled_buffer_4
  and and_9 (and_9_out, not_1_out, not_5_out, not_4_out);
  not not_4 (not_4_out, jump);
  not not_5 (not_5_out, jumpreg);
  assign nPC_sel = branch ? 2'b01 : 2'bz;  // Controlled_Buffer controlled_buffer_5
  assign nPC_sel = jump ? 2'b10 : 2'bz;  // Controlled_Buffer controlled_buffer_6
  assign nPC_sel = jumpreg ? 2'b11 : 2'bz;  // Controlled_Buffer controlled_buffer_7
  or or_5 (cutoff, beq, bne, beqinc, j, jr, jal, jalr);
  or or_6 (or_6_out, sll, lui);
  or or_7 (or_7_out, MemtoReg, add, MemWr, addi);
  or or_8 (or_8_out, beq, beqinc);
  assign ALUctr = or_6_out ? 4'b0000 : 4'bz;  // Controlled_Buffer controlled_buffer_8
  assign ALUctr = srl ? 4'b0001 : 4'bz;  // Controlled_Buffer controlled_buffer_9
  assign ALUctr = sra ? 4'b0010 : 4'bz;  // Controlled_Buffer controlled_buffer_10
  assign ALUctr = mult ? 4'b0011 : 4'bz;  // Controlled_Buffer controlled_buffer_11
  assign ALUctr = divu ? 4'b0100 : 4'bz;  // Controlled_Buffer controlled_buffer_12
  assign ALUctr = or_7_out ? 4'b0101 : 4'bz;  // Controlled_Buffer controlled_buffer_13
  assign ALUctr = or_9_out ? 4'b0110 : 4'bz;  // Controlled_Buffer controlled_buffer_14
  or or_9 (or_9_out, addu, addiu, increment);
  and and_10 (and_10_out, or_8_out, equal);
  and and_11 (and_11_out, bne, ~equal);  // AND_Gate
  or or_10 (jumpreg, jr, jalr);
  or or_11 (jump, j, jal);
  or or_12 (shift, sll, srl, sra);
  assign ALUctr = sub ? 4'b0111 : 4'bz;  // Controlled_Buffer controlled_buffer_15
  assign ALUctr = subu ? 4'b1000 : 4'bz;  // Controlled_Buffer controlled_buffer_16
  or or_13 (or_13_out, \or , ori);
  or or_14 (or_14_out, \xor , xori);
  or or_15 (branch, and_10_out, and_11_out);
  assign ALUctr = or_16_out ? 4'b1001 : 4'bz;  // Controlled_Buffer controlled_buffer_17
  or or_16 (or_16_out, \and , andi);
  assign ALUctr = or_13_out ? 4'b1010 : 4'bz;  // Controlled_Buffer controlled_buffer_18
  assign ALUctr = or_14_out ? 4'b1011 : 4'bz;  // Controlled_Buffer controlled_buffer_19
  assign ALUctr = \nor  ? 4'b1100 : 4'bz;  // Controlled_Buffer controlled_buffer_20
  assign ALUctr = or_17_out ? 4'b1101 : 4'bz;  // Controlled_Buffer controlled_buffer_21
  or or_17 (or_17_out, slt, slti);
  assign ALUctr = or_18_out ? 4'b1110 : 4'bz;  // Controlled_Buffer controlled_buffer_22
  or or_18 (or_18_out, sltu, sltiu);
  and and_12 (increment, beqinc, ~equal);  // AND_Gate

  // Other names for the same wires on the sheet: i_type = ALUSrc; lw = MemtoReg; sw = MemWr
endmodule
