// Logisim project regfile.circ as structural Verilog: 1 circuit, main circuit main
module main (
  input  [4:0] Read_Register_1,
  input  [4:0] Read_Register_2,
  input  [4:0] Write_Register,
  input  [31:0] Write_Data,
  input  Write_Enable,
  input  Clock,
  output [31:0] s0_Value,
  output [31:0] s1_Value,
  output [31:0] s2_Value,
  output [31:0] ra_Value,
  output [31:0] sp_Value,
  output [31:0] Read_Data_1,
  output [31:0] Read_Data_2
);

  wire [31:0] i1, i2, i3, i4, i5, i6, i7, i8, i9, i10, i11, i12, i13, i14, i15, i16, i17, i18, i19, i20, i21,
       i22, i23, i24, i25, i26, i27, i28, i29, i30, i31, i32, o1, o2, o3, o4, o5, o6, o7, o8, o9, o10, o11,
       o12, o13, o14, o15, o16, o20, o21, o22, o23, o24, o25, o26, o27, o28, o29, o31;

  Register #(.width(32)) register_1 (.D({32{1'b0}}), .Q(o1), .clk(Clock));  // open: en, clr
  Register #(.width(32)) register_2 (.D(i5), .Q(o5), .clk(Clock));  // open: en, clr
  Register #(.width(32)) register_3 (.D(i9), .Q(o9), .clk(Clock));  // open: en, clr
  Register #(.width(32)) register_4 (.D(i13), .Q(o13), .clk(Clock));  // open: en, clr
  Register #(.width(32)) register_5 (.D(i17), .Q(s0_Value), .clk(Clock));  // open: en, clr
  Register #(.width(32)) register_6 (.D(i21), .Q(o21), .clk(Clock));  // open: en, clr
  Register #(.width(32)) register_7 (.D(i25), .Q(o25), .clk(Clock));  // open: en, clr
  Register #(.width(32)) register_8 (.D(i29), .Q(o29), .clk(Clock));  // open: en, clr
  Register #(.width(32)) register_9 (.D(i2), .Q(o2), .clk(Clock));  // open: en, clr
  Register #(.width(32)) register_10 (.D(i6), .Q(o6), .clk(Clock));  // open: en, clr
  Register #(.width(32)) register_11 (.D(i10), .Q(o10), .clk(Clock));  // open: en, clr
  Register #(.width(32)) register_12 (.D(i14), .Q(o14), .clk(Clock));  // open: en, clr
  Register #(.width(32)) register_13 (.D(i18), .Q(s1_Value), .clk(Clock));  // open: en, clr
  Register #(.width(32)) register_14 (.D(i22), .Q(o22), .clk(Clock));  // open: en, clr
  Register #(.width(32)) register_15 (.D(i26), .Q(o26), .clk(Clock));  // open: en, clr
  Register #(.width(32)) register_16 (.D(i30), .Q(sp_Value), .clk(Clock));  // open: en, clr
  Register #(.width(32)) register_17 (.D(i3), .Q(o3), .clk(Clock));  // open: en, clr
  Register #(.width(32)) register_18 (.D(i7), .Q(o7), .clk(Clock));  // open: en, clr
  Register #(.width(32)) register_19 (.D(i11), .Q(o11), .clk(Clock));  // open: en, clr
  Register #(.width(32)) register_20 (.D(i15), .Q(o15), .clk(Clock));  // open: en, clr
  Register #(.width(32)) register_21 (.D(i19), .Q(s2_Value), .clk(Clock));  // open: en, clr
  Register #(.width(32)) register_22 (.D(i23), .Q(o23), .clk(Clock));  // open: en, clr
  Register #(.width(32)) register_23 (.D(i27), .Q(o27), .clk(Clock));  // open: en, clr
  Register #(.width(32)) register_24 (.D(i31), .Q(o31), .clk(Clock));  // open: en, clr
  Register #(.width(32)) register_25 (.D(i4), .Q(o4), .clk(Clock));  // open: en, clr
  Register #(.width(32)) register_26 (.D(i8), .Q(o8), .clk(Clock));  // open: en, clr
  Register #(.width(32)) register_27 (.D(i12), .Q(o12), .clk(Clock));  // open: en, clr
  Register #(.width(32)) register_28 (.D(i16), .Q(o16), .clk(Clock));  // open: en, clr
  Register #(.width(32)) register_29 (.D(i20), .Q(o20), .clk(Clock));  // open: en, clr
  Register #(.width(32)) register_30 (.D(i24), .Q(o24), .clk(Clock));  // open: en, clr
  Register #(.width(32)) register_31 (.D(i28), .Q(o28), .clk(Clock));  // open: en, clr
  Register #(.width(32)) register_32 (.D(i32), .Q(ra_Value), .clk(Clock));  // open: en, clr
  Multiplexer #(.select(5), .width(32)) multiplexer_1 (
    .in0(o1), .in1(o2), .in2(o3), .in3(o4), .in4(o5), .in5(o6), .in6(o7), .in7(o8), .in8(o9), .in9(o10),
    .in10(o11), .in11(o12), .in12(o13), .in13(o14), .in14(o15), .in15(o16), .in16(s0_Value), .in17(s1_Value),
    .in18(s2_Value), .in19(o20), .in20(o21), .in21(o22), .in22(o23), .in23(o24), .in24(o25), .in25(o26),
    .in26(o27), .in27(o28), .in28(o29), .in29(sp_Value), .in30(o31), .in31(ra_Value), .out(Read_Data_1),
    .sel(Read_Register_1));  // open: en
  Demultiplexer #(.select(5), .width(32), .tristate("true")) demultiplexer_1 (
    .out0(i1), .out1(i2), .out2(i3), .out3(i4), .out4(i5), .out5(i6), .out6(i7), .out7(i8), .out8(i9),
    .out9(i10), .out10(i11), .out11(i12), .out12(i13), .out13(i14), .out14(i15), .out15(i16), .out16(i17),
    .out17(i18), .out18(i19), .out19(i20), .out20(i21), .out21(i22), .out22(i23), .out23(i24), .out24(i25),
    .out25(i26), .out26(i27), .out27(i28), .out29(i29), .out30(i31), .out31(i32), .in(Write_Data),
    .sel(Write_Register), .en(Write_Enable));  // open: out28
  Multiplexer #(.select(5), .width(32)) multiplexer_2 (
    .in0(o1), .in1(o2), .in2(o3), .in3(o4), .in4(o5), .in5(o6), .in6(o7), .in7(o8), .in8(o9), .in9(o10),
    .in10(o11), .in11(o12), .in12(o13), .in13(o14), .in14(o15), .in15(o16), .in16(s0_Value), .in17(s1_Value),
    .in18(s2_Value), .in19(o20), .in20(o21), .in21(o22), .in22(o23), .in23(o24), .in24(o25), .in25(o26),
    .in26(o27), .in27(o28), .in28(o29), .in29(sp_Value), .in30(o31), .in31(ra_Value), .out(Read_Data_2),
    .sel(Read_Register_2));  // open: en

  // Other names for the same wires on the sheet: clk = Clock; o17[31:0] = s0_Value; o18[31:0] = s1_Value;
  //   o19[31:0] = s2_Value; o30[31:0] = sp_Value; o32[31:0] = ra_Value; read_data1[31:0] = Read_Data_1;
  //   read_data2[31:0] = Read_Data_2; read_reg1[4:0] = Read_Register_1; read_reg2[4:0] = Read_Register_2;
  //   write_en = Write_Enable; write_reg[4:0] = Write_Register

  // Notes on the sheet:
  //   INPUTS to your circuit
  //   DON'T CHANGE THE LOCATIONS OF THE INPUTS AND OUTPUTS!
  //   R1
  //   R5
  //   R9
  //   R13
  //   R17
  //   R21
  //   R25
  //   R29
  //   R2
  //   R6
  //   R10
  //   R14
  //   R18
  //   R22
  //   R26
  //   R30
  //   R3
  //   R7
  //   R11
  //   R15
  //   R19
  //   R23
  //   R27
  //   R31
  //   These are DEBUG/TEST outputs from your circuit.
  //   R4
  //   R8
  //   R12
  //   R16
  //   R20
  //   R24
  //   R28
  //   R32
  //   OUTPUTS from your circuit
endmodule
